# Fritzing sketch Homing (saved by Fritzing 1.0.5)
breadboards: 1

parts:
  Mod1 = Amica NodeMCU DEVKIT 1.0
  SERVO1 = Tower Pro SG90 servo [part_number=101246]
  SERVO2 = Tower Pro SG90 servo [part_number=101246]
  Part1 = Adafruit TCS34725 RGB Color Sensor [part_number="Adafruit #1334"]

nets:
  N1: Mod1.pin1, Mod1.pin_10, Mod1.pin_26
  GND: Mod1.pin2, Mod1.pin_9, Mod1.pin_25, Mod1.pin_29, SERVO1.GND, SERVO2.GND, Part1.GND
  N2: Mod1.pin7, SERVO2.Signal
  N3: Mod1.pin8, SERVO1.Signal
  N4: Mod1.pin_13, Part1.SCL
  N5: Mod1.pin_14, Part1.SDA
  +5V: Mod1.pin_30, SERVO1.+5V, SERVO2.+5V, Part1.VIN

custom parts:
  Tower Pro SG90 servo: Original file by John De Cristofaro http://www.adafruit.com/products/1449 Adafruit Feedback Servo (Small) Edited by: e-radionica.com 28/9/2015
  Adafruit TCS34725 RGB Color Sensor: Your electronics can now see in dazzling color with this lovely color light sensor. We found the best color sensor on the market, the TCS34725, which has RGB and Clear light sensing elements. An IR blocking filter, integrated on-chip and localized to the color sensing photodiodes, minimizes the IR spectral component of the incoming light and allows color measurements to be made accurately. The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
