# Fritzing sketch Colour Sensor - Chameleon (saved by Fritzing 1.0.5)
breadboards: 1

parts:
  Mod1 = Amica NodeMCU DEVKIT 1.0
  U1 = Barometric Pressure Sensor
  Mod2 = KY-016 RGB Full Color LED Module [package="Breakout board"]

nets:
  N1: Mod1.pin1, Mod1.pin_10, Mod1.pin_26
  N2: Mod1.pin2, Mod1.pin_9, Mod1.pin_25, Mod1.pin_29, U1.3.3V, Mod2.-
  N3: Mod1.pin5, Mod2.G
  N4: Mod1.pin6, Mod2.R
  N5: Mod1.pin_12, Mod2.B
  N6: Mod1.pin_13, U1.MOSI
  N7: Mod1.pin_14, U1.MISO
  N8: Mod1.pin_30, U1.GND

custom parts:
  KY-016 RGB Full Color LED Module: KY-016 Arduino full color 5mm RGB LED, different colors can be obtained by mixing the three primary colors.
