# Fritzing sketch Homing (saved by Fritzing 1.0.5)
breadboards: 1

parts:
  Mod1 = Amica NodeMCU DEVKIT 1.0
  SERVO1 = Tower Pro SG90 servo [part_number=101246]
  SERVO2 = Tower Pro SG90 servo [part_number=101246]

nets:
  N1: Mod1.pin1, Mod1.pin_10, Mod1.pin_26
  GND: Mod1.pin2, Mod1.pin_9, Mod1.pin_25, Mod1.pin_29, SERVO1.GND, SERVO2.GND
  +5V: Mod1.pin_30, SERVO1.+5V, SERVO2.+5V

custom parts:
  Tower Pro SG90 servo: Original file by John De Cristofaro http://www.adafruit.com/products/1449 Adafruit Feedback Servo (Small) Edited by: e-radionica.com 28/9/2015
